# Fritzing sketch embs (saved by Fritzing 0.9.3b)
breadboards: 1

parts:
  M1 = MAX30102
  Composant1 = Arduino Mega ADK (Rev3)
  DHT1 = Humidity and Temperature Sensor DHT11
  Composant4 = Triple Axis Accelerometer Breakout - ADXL335
  Mod1 = AD8232 HeartRate Monitor [part_number=SEN-12650]
  Gizwits_WiFi_Witty_ESP-12F1 = Gizwits WiFi Witty ESP-12F
  IC1 = MQ-2 [package="DIP (Dual Inline) [THT]"]

nets:
  VCC: M1.VIN, Composant1.IOREF, Composant1.5V, DHT1.Vcc, Composant4.VCC, Gizwits_WiFi_Witty_ESP-12F1.VCC, IC1.pin1
  N1: M1.SCL, Composant1.D21/SCL
  N2: M1.SDA, Composant1.D20/SDA
  GND: M1.GND, Composant1.GND, DHT1.GND_2, Composant4.GND, Mod1.GND, Gizwits_WiFi_Witty_ESP-12F1.GND, IC1.pin2
  N3: Composant1.A8, Composant4.YOUT
  N4: Composant1.A0, Mod1.OUTPUT
  N5: Composant1.A4, IC1.pin4
  N6: Composant1.A5, Composant4.XOUT
  N7: Composant1.A7, Composant4.ZOUT
  N8: Composant1.D18/TX1, Gizwits_WiFi_Witty_ESP-12F1.RXD
  N9: Composant1.D11_PWM, Mod1.LO-
  N10: Composant1.D10_PWM, Mod1.LO+
  3V3: Composant1.3V3, Mod1.3.3v

custom parts:
  MAX30102: Oximeter module using the MAX30102 chip. You may wish to read (and check your module) this post on power problems with these modules: https://reedpaper.wordpress.com/2018/08/22/pulse-oximeter-max30100-max30102-how-to-fix-wrong-board/ . As usual, if you want the mounting holes in pcb, you need to drag a hole over the pad in silkscreen to actually drill the hole (by default they are not drilled)
  Humidity and Temperature Sensor DHT11: Digital relative humidity & temperature sensor DHT11
  AD8232 HeartRate Monitor: Sparkfun single lead heart rate monitor - Ad8232.
  MQ-2: MQ-2 Gas Sensor module
